// Logisim project MpMp25.circ as structural Verilog: 3 circuits, main circuit main
module main (
  output [7:0] out_1
);

  ALU alu_1 (.Op0(8'h2), .Op1(8'h3), .CMD_15_12(4'b0000), .Result(out_1));
endmodule

module ALU (
  input  [7:0] Op0,
  input  [7:0] Op1,
  input  [3:0] CMD_15_12,
  output [7:0] Result
);

  wire [7:0] adder_1_out, subtractor_1_out;

  Adder adder_1 (.a(Op0), .b(Op1), .out(adder_1_out));  // open: cin, cout
  Subtractor subtractor_1 (.a(Op1), .b(Op0), .out(subtractor_1_out));  // open: bin, bout
  Multiplexer #(.select(4), .width(8)) multiplexer_1 (
    .in0(adder_1_out), .in1(subtractor_1_out), .out(Result), .sel(CMD_15_12));  // open: in2, in3, in4, in5, in6, in7, in8, in9, in10, in11, in12, in13, in14, in15
endmodule

module CU (
  input  CLK,
  input  RST,
  input  [15:0] Instruction
);

  wire [1:0] Cyclecounter_q;
  wire [15:0] register_1_q;

  Register #(.width(16)) register_1 (.D(Instruction), .clk(CLK), .Q(register_1_q), .clr(RST));  // open: en
  Counter #(.max('h3), .width(2)) Cyclecounter (
    .Q(Cyclecounter_q), .clk(CLK), .clr(RST));  // open: load, D, count, carry, up
  ROM #(.addrWidth(9), .dataWidth(32)) rom_1 (.addr({register_1_q[7], register_1_q[11], register_1_q[6], register_1_q[15:12], Cyclecounter_q}));  // open: data

  // Notes on the sheet:
  //   IMOPb[7]
  //   IMOPa[11]
  //   CMD[6]
  //   CMD0[15...12]
endmodule
